# Fritzing sketch spieed doc (saved by Fritzing 0.9.4)

parts:
  U1 = ESP32-38PinWide [part_number=ESP32-38PinWide]
  J1 = Basic Servo
  Part1 = Sipeed doc  # not connected
  Part3 = Sipeed doc  # not connected
  VCC1 = 4 x AAA Battery Mount  # not connected

nets:
  N1: U1.GPIO14, J1.pulse

notes:
  5volts dc
  D5 from esp connects to D1of spieed
  signal of servo conected to D14
  D13 of Spieed conected to D34 of Esp32
  5v and gnd from Spieed Doc

custom parts:
  ESP32-38PinWide: Generic 38-Pin ESP32 with wide format (only access to one side of pins on a breadboard) based on Stephen Lilley's HiLetgo ESP-WROOM-32 ESP32 ESP-32S Development Board.
  Sipeed doc: The Arduino Uno is a microcontroller board based on the ATmega328 (datasheet). It has 14 digital input/output pins (of which 6 can be used as PWM outputs), 6 analog inputs, a 16 MHz ceramic resonator, a USB connection, a power jack, an ICSP header, and a reset button. It contains everything needed to support the microcontroller; simply connect it to a computer with a USB cable or power it with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
